// Logisim project release.circ as structural Verilog
module SUBCIRC_MatrixMultiplier (
  input  [63:0] B0,
  input  [63:0] A0,
  input  [63:0] B1,
  input  [63:0] A1,
  input  [63:0] B2,
  input  [63:0] A2,
  input  [63:0] B3,
  input  [63:0] A3,
  output [63:0] S0,
  output [63:0] S1,
  output [63:0] S2,
  output [63:0] S3,
  output [63:0] W0,
  output [63:0] W1,
  output [63:0] W2,
  output [63:0] W3
);

  Multiplier #(.width(64)) multiplier_1 (.a(A0), .b(B0), .out(S0));  // open: cin, cout
  Multiplier #(.width(64)) multiplier_2 (.a(A0), .b(B1), .out(S1));  // open: cin, cout
  Multiplier #(.width(64)) multiplier_3 (.a(A2), .b(B0), .out(S2));  // open: cin, cout
  Multiplier #(.width(64)) multiplier_4 (.a(A2), .b(B1), .out(S3));  // open: cin, cout
  Multiplier #(.width(64)) multiplier_5 (.a(A1), .b(B2), .out(W0));  // open: cin, cout
  Multiplier #(.width(64)) multiplier_6 (.a(A1), .b(B3), .out(W1));  // open: cin, cout
  Multiplier #(.width(64)) multiplier_7 (.a(A3), .b(B2), .out(W2));  // open: cin, cout
  Multiplier #(.width(64)) multiplier_8 (.a(A3), .b(B3), .out(W3));  // open: cin, cout

  // Notes on the sheet:
  //   Acts as a Partial Multiplication Node
  //   Supports Partial Matrix Multiplication where A*B = S1, S2 where S = S1+S2
  //   A0B0
  //   A0B1
  //   A2B0
  //   A2B1
  //   A1B2
  //   A1B3
  //   A3B2
  //   A3B3
endmodule

module RAMControllerRAW (
  input  [7:0] rs,
  input  [7:0] rd,
  input  CLK,
  output [7:0] A,
  output WE,
  output OE
);

  D_Flip_Flop d_ff_1 (.clk(CLK), .D(1'b1), .Q(WE));  // open: Qn, preset, reset
  not not_1 (OE, CLK);
  Multiplexer #(.width(8)) multiplexer_1 (.in0(rs), .in1(rd), .out(A), .sel(CLK));
endmodule

module SUBCIRC_RAMBank (
  input  [63:0] D3,
  input  [63:0] D2,
  input  [63:0] D1,
  input  [63:0] D0,
  input  [7:0] Address,
  input  WE,
  input  OE,
  input  CLK,
  output [63:0] S3,
  output [63:0] S2,
  output [63:0] S1,
  output [63:0] S0
);

  RAM #(.asyncread("true"), .dataWidth(64), .trigger("falling"), .\type ("nonvolatile")) C1 (
    .addr(Address), .we(WE), .oe(OE), .clk(CLK), .din(D0), .dout(S0));
  RAM #(.asyncread("true"), .dataWidth(64), .trigger("falling"), .\type ("nonvolatile")) ram_1 (
    .addr(Address), .we(WE), .oe(OE), .clk(CLK), .din(D1), .dout(S1));
  RAM #(.asyncread("true"), .dataWidth(64), .trigger("falling"), .\type ("nonvolatile")) ram_2 (
    .addr(Address), .we(WE), .oe(OE), .clk(CLK), .din(D2), .dout(S2));
  RAM #(.asyncread("true"), .dataWidth(64), .trigger("falling"), .\type ("nonvolatile")) ram_3 (
    .addr(Address), .we(WE), .oe(OE), .clk(CLK), .din(D3), .dout(S3));
endmodule

module Assembly (
);

  wire CLOCK_GLOBAL, ITERCOUNT, ramcontrollerraw_1_oe, ramcontrollerraw_1_we;
  wire [1:1] ram_1_dout;
  wire [7:0] counter_1_q, ramcontrollerraw_1_a, register_1_q, undriven;
  wire [63:0] subcirc_matrixadder_1_s0, subcirc_matrixadder_1_s1, subcirc_matrixadder_1_s2,
       subcirc_matrixadder_1_s3, subcirc_rambank_1_s0, subcirc_rambank_1_s1, subcirc_rambank_1_s2,
       subcirc_rambank_1_s3, subcirc_rambank_2_s0, subcirc_rambank_2_s1, subcirc_rambank_2_s2,
       subcirc_rambank_2_s3, subcirc_rambank_3_s0, subcirc_rambank_3_s1, subcirc_rambank_3_s2,
       subcirc_rambank_3_s3, subcirc_rambank_4_s0, subcirc_rambank_4_s1, subcirc_rambank_4_s2,
       subcirc_rambank_4_s3, undriven_2, undriven_3, undriven_4, undriven_5;

  Counter counter_1 (.count(1'b1), .Q(counter_1_q), .up(1'b1), .clk(CLOCK_GLOBAL));  // open: load, D, carry, clr
  RAMControllerRAW ramcontrollerraw_1 (
    .rs(counter_1_q), .rd(undriven), .CLK(CLOCK_GLOBAL), .A(ramcontrollerraw_1_a),
    .WE(ramcontrollerraw_1_we), .OE(ramcontrollerraw_1_oe));
  Counter counter_2 ();  // open: load, D, count, Q, carry, up, clk, clr
  // Probe on subcirc_matrixadder_1_s3
  // Probe on subcirc_matrixadder_1_s1
  SUBCIRC_RAMBank subcirc_rambank_1 (
    .Address(ramcontrollerraw_1_a), .WE(ramcontrollerraw_1_we), .OE(ramcontrollerraw_1_oe),
    .CLK(CLOCK_GLOBAL), .S3(subcirc_rambank_1_s3), .S2(subcirc_rambank_1_s2), .S1(subcirc_rambank_1_s1),
    .S0(subcirc_rambank_1_s0));  // open: D3, D2, D1, D0
  SUBCIRC_RAMBank subcirc_rambank_2 (
    .Address(ramcontrollerraw_1_a), .WE(ramcontrollerraw_1_we), .OE(ramcontrollerraw_1_oe),
    .CLK(CLOCK_GLOBAL), .S3(subcirc_rambank_2_s3), .S2(subcirc_rambank_2_s2), .S1(subcirc_rambank_2_s1),
    .S0(subcirc_rambank_2_s0));  // open: D3, D2, D1, D0
  SUBCIRC_MatrixAdder subcirc_matrixadder_1 (
    .S0(subcirc_matrixadder_1_s0), .S1(subcirc_matrixadder_1_s1), .S2(subcirc_matrixadder_1_s2),
    .S3(subcirc_matrixadder_1_s3));  // open: B0, A0, B1, A1, B2, A2, B3, A3
  // Probe on subcirc_matrixadder_1_s2
  // Probe on subcirc_matrixadder_1_s0
  SUBCIRC_RAMBank subcirc_rambank_3 (
    .Address(ramcontrollerraw_1_a), .WE(ramcontrollerraw_1_we), .OE(ramcontrollerraw_1_oe),
    .CLK(CLOCK_GLOBAL), .S3(subcirc_rambank_3_s3), .S2(subcirc_rambank_3_s2), .S1(subcirc_rambank_3_s1),
    .S0(subcirc_rambank_3_s0));  // open: D3, D2, D1, D0
  SUBCIRC_RAMBank subcirc_rambank_4 (
    .Address(ramcontrollerraw_1_a), .WE(ramcontrollerraw_1_we), .OE(ramcontrollerraw_1_oe),
    .CLK(CLOCK_GLOBAL), .S3(subcirc_rambank_4_s3), .S2(subcirc_rambank_4_s2), .S1(subcirc_rambank_4_s1),
    .S0(subcirc_rambank_4_s0));  // open: D3, D2, D1, D0
  Register register_1 (.D(ramcontrollerraw_1_a), .en(1'b1), .Q(register_1_q), .clk(CLOCK_GLOBAL));  // open: clr
  Clock clock_1 (.out(CLOCK_GLOBAL));
  SUBCIRC_RAMBank subcirc_rambank_5 (
    .D3(undriven_2), .D2(undriven_3), .D1(undriven_4), .D0(undriven_5), .Address(register_1_q),
    .CLK(CLOCK_GLOBAL));  // open: WE, OE, S3, S2, S1, S0
  RAM #(.addrWidth(2), .dataWidth(2)) ram_1 (
    .addr(2'b00), .oe(1'b1), .clk(CLOCK_GLOBAL), .dout({ram_1_dout[1], ITERCOUNT}));  // open: we, din

  // Notes on the sheet:
  //   Pipelined
  //   Constant High Bit
  //   Row[0]
  //   Row[1]
  //   A
  //   Col[0]
  //   Col[1]
  //   B
  //   O
  //   Configuration RAM, Holds Matrix Size (N/4)[0], Data Type (0: int64, 1: float64)[1]
endmodule

module SUBCIRC_MatrixAdder (
  input  [63:0] B0,
  input  [63:0] A0,
  input  [63:0] B1,
  input  [63:0] A1,
  input  [63:0] B2,
  input  [63:0] A2,
  input  [63:0] B3,
  input  [63:0] A3,
  output [63:0] S0,
  output [63:0] S1,
  output [63:0] S2,
  output [63:0] S3
);

  Adder #(.width(64)) adder_1 (.a(B0), .b(A0), .out(S0));  // open: cin, cout
  Adder #(.width(64)) adder_2 (.a(B1), .b(A1), .out(S1));  // open: cin, cout
  Adder #(.width(64)) adder_3 (.a(B2), .b(A2), .out(S2));  // open: cin, cout
  Adder #(.width(64)) adder_4 (.a(B3), .b(A3), .out(S3));  // open: cin, cout

  // Notes on the sheet:
  //   Acts as a Addition Node
endmodule

module TEST_MatrixMultiplier (
);

  wire [63:0] subcirc_matrixadder_1_s0, subcirc_matrixadder_1_s1, subcirc_matrixadder_1_s2,
       subcirc_matrixadder_1_s3, subcirc_matrixmultiplier_1_s0, subcirc_matrixmultiplier_1_s1,
       subcirc_matrixmultiplier_1_s2, subcirc_matrixmultiplier_1_s3, subcirc_matrixmultiplier_1_w0,
       subcirc_matrixmultiplier_1_w1, subcirc_matrixmultiplier_1_w2, subcirc_matrixmultiplier_1_w3;

  SUBCIRC_MatrixMultiplier subcirc_matrixmultiplier_1 (
    .B0(64'h5), .A0(64'h1), .B1(64'h6), .A1(64'h2), .B2(64'h7), .A2(64'h3), .B3(64'h8), .A3(64'h4),
    .S0(subcirc_matrixmultiplier_1_s0), .S1(subcirc_matrixmultiplier_1_s1),
    .S2(subcirc_matrixmultiplier_1_s2), .S3(subcirc_matrixmultiplier_1_s3),
    .W0(subcirc_matrixmultiplier_1_w0), .W1(subcirc_matrixmultiplier_1_w1),
    .W2(subcirc_matrixmultiplier_1_w2), .W3(subcirc_matrixmultiplier_1_w3));
  SUBCIRC_MatrixAdder subcirc_matrixadder_1 (
    .B0(subcirc_matrixmultiplier_1_s0), .A0(subcirc_matrixmultiplier_1_w0),
    .B1(subcirc_matrixmultiplier_1_s1), .A1(subcirc_matrixmultiplier_1_w1),
    .B2(subcirc_matrixmultiplier_1_s2), .A2(subcirc_matrixmultiplier_1_w2),
    .B3(subcirc_matrixmultiplier_1_s3), .A3(subcirc_matrixmultiplier_1_w3), .S0(subcirc_matrixadder_1_s0),
    .S1(subcirc_matrixadder_1_s1), .S2(subcirc_matrixadder_1_s2), .S3(subcirc_matrixadder_1_s3));
  // Probe on subcirc_matrixadder_1_s0
  // Probe on subcirc_matrixadder_1_s2
  // Probe on subcirc_matrixadder_1_s1
  // Probe on subcirc_matrixadder_1_s3

  // Notes on the sheet:
  //   Subcircuit works perfectly for 2x2 Matrix Multiplicaton / Verified on multiple data with overflow
endmodule

module WorkBench (
);

  wire clock_1_out, clock_2_out;
  wire [7:0] counter_1_q, counter_2_q;
  wire [63:0] adder_1_out, adder_2_out, multiplier_1_out, multiplier_2_out, ram_1_dout, ram_2_dout,
       ram_3_dout, ram_4_dout, register_1_q, register_2_q;

  Clock clock_1 (.out(clock_1_out));
  RAM #(.dataWidth(64), .\type ("nonvolatile")) ram_1 (
    .addr(counter_1_q), .oe(1'b1), .clk(clock_1_out), .dout(ram_1_dout));  // open: we, din
  Counter counter_1 (.count(1'b1), .Q(counter_1_q), .up(1'b1), .clk(clock_1_out));  // open: load, D, carry, clr
  RAM #(.dataWidth(64), .\type ("nonvolatile")) ram_2 (
    .addr(counter_1_q), .oe(1'b1), .clk(clock_1_out), .dout(ram_2_dout));  // open: we, din
  Multiplier #(.width(64)) multiplier_1 (.a(ram_1_dout), .b(ram_2_dout), .out(multiplier_1_out));  // open: cin, cout
  Register #(.width(64)) register_1 (
    .D(multiplier_1_out), .en(1'b1), .Q(register_1_q), .clk(clock_1_out));  // open: clr
  Adder #(.width(64)) adder_1 (.a(register_1_q), .b(multiplier_1_out), .out(adder_1_out));  // open: cin, cout
  // Probe on adder_1_out
  Clock clock_2 (.out(clock_2_out));
  RAM #(.dataWidth(64), .\type ("nonvolatile")) ram_3 (
    .addr(counter_2_q), .oe(1'b1), .clk(clock_2_out), .dout(ram_3_dout));  // open: we, din
  Counter counter_2 (.count(1'b1), .Q(counter_2_q), .up(1'b1), .clk(clock_2_out));  // open: load, D, carry, clr
  RAM #(.dataWidth(64), .\type ("nonvolatile")) ram_4 (
    .addr(counter_2_q), .oe(1'b1), .clk(clock_2_out), .dout(ram_4_dout));  // open: we, din
  Multiplier #(.width(64)) multiplier_2 (.a(ram_3_dout), .b(ram_4_dout), .out(multiplier_2_out));  // open: cin, cout
  Register #(.width(64)) register_2 (
    .D(multiplier_2_out), .en(1'b1), .Q(register_2_q), .clk(clock_2_out));  // open: clr
  Adder #(.width(64)) adder_2 (.a(register_2_q), .b(multiplier_2_out), .out(adder_2_out));  // open: cin, cout
  // Probe on adder_2_out

  // Notes on the sheet:
  //   AB;CD
  //   A
  //   WX;YZ
  //   B
  //   AB;CD
  //   A
  //   WX;YZ
  //   B
endmodule

module RAMController (
  input  [7:0] rs,
  input  [7:0] rd,
  input  CLK,
  output [7:0] A,
  output WE,
  output OE
);

  D_Flip_Flop d_ff_1 (.clk(CLK), .D(1'b1), .Q(WE));  // open: Qn, preset, reset
  not not_1 (OE, CLK);
  Multiplexer #(.width(8)) multiplexer_1 (.in0(rs), .in1(rd), .out(A), .sel(CLK));
endmodule
