// Logisim project release_v2.circ as structural Verilog
module DEPRECATED_RegisterBankEdged (
  input  [63:0] D3,
  input  [63:0] D2,
  input  [63:0] D1,
  input  [63:0] D0,
  input  CLEAR,
  input  CLK,
  input  EN3,
  input  EN2,
  input  EN1,
  input  EN0,
  output [63:0] S3,
  output [63:0] S2,
  output [63:0] S1,
  output [63:0] S0
);

  Register #(.width(64)) register_1 (.D(D3), .en(EN3), .Q(S3), .clk(CLK), .clr(CLEAR));
  Register #(.trigger("falling"), .width(64)) register_2 (.D(D2), .en(EN2), .Q(S2), .clk(CLK), .clr(CLEAR));
  Register #(.width(64)) register_3 (.D(D1), .en(EN1), .Q(S1), .clk(CLK), .clr(CLEAR));
  Register #(.trigger("falling"), .width(64)) register_4 (.D(D0), .en(EN0), .Q(S0), .clk(CLK), .clr(CLEAR));
endmodule

module Accumulator (
  input  Clear,
  input  Enable,
  input  CLK,
  input  [63:0] A0,
  input  [63:0] A1,
  input  [63:0] A2,
  input  [63:0] A3,
  output [63:0] S0,
  output [63:0] S1,
  output [63:0] S2,
  output [63:0] S3
);

  wire [63:0] matrixadder_1_s0, matrixadder_1_s1, matrixadder_1_s2, matrixadder_1_s3;

  Register #(.width(64)) register_1 (.D(matrixadder_1_s3), .en(Enable), .Q(S0), .clk(CLK), .clr(Clear));
  Register #(.width(64)) register_2 (.D(matrixadder_1_s2), .en(Enable), .Q(S1), .clk(CLK), .clr(Clear));
  Register #(.width(64)) register_3 (.D(matrixadder_1_s1), .en(Enable), .Q(S2), .clk(CLK), .clr(Clear));
  Register #(.width(64)) register_4 (.D(matrixadder_1_s0), .en(Enable), .Q(S3), .clk(CLK), .clr(Clear));
  MatrixAdder matrixadder_1 (
    .B0(S0), .B1(S1), .B2(S2), .B3(S3), .A0(A0), .A1(A1), .A2(A2), .A3(A3), .S0(matrixadder_1_s0),
    .S1(matrixadder_1_s1), .S2(matrixadder_1_s2), .S3(matrixadder_1_s3));
endmodule

module MatrixMultiplier (
  input  [63:0] A3,
  input  [63:0] A2,
  input  [63:0] A1,
  input  [63:0] A0,
  input  GAP,
  input  [63:0] B3,
  input  [63:0] B2,
  input  [63:0] B1,
  input  [63:0] B0,
  output [63:0] S0,
  output [63:0] S1,
  output [63:0] S2,
  output [63:0] S3,
  output [63:0] W0,
  output [63:0] W1,
  output [63:0] W2,
  output [63:0] W3
);

  Multiplier #(.width(64)) multiplier_1 (.a(A0), .b(B0), .out(S0));  // open: cin, cout
  Multiplier #(.width(64)) multiplier_2 (.a(A0), .b(B1), .out(S1));  // open: cin, cout
  Multiplier #(.width(64)) multiplier_3 (.a(A2), .b(B0), .out(S2));  // open: cin, cout
  Multiplier #(.width(64)) multiplier_4 (.a(A2), .b(B1), .out(S3));  // open: cin, cout
  Multiplier #(.width(64)) multiplier_5 (.a(A1), .b(B2), .out(W0));  // open: cin, cout
  Multiplier #(.width(64)) multiplier_6 (.a(A1), .b(B3), .out(W1));  // open: cin, cout
  Multiplier #(.width(64)) multiplier_7 (.a(A3), .b(B2), .out(W2));  // open: cin, cout
  Multiplier #(.width(64)) multiplier_8 (.a(A3), .b(B3), .out(W3));  // open: cin, cout

  // Notes on the sheet:
  //   Acts as a Partial Multiplication Node
  //   Supports Partial Matrix Multiplication where A*B = S1, S2 where S = S1+S2
  //   A0B0
  //   A0B1
  //   A2B0
  //   A2B1
  //   A1B2
  //   A1B3
  //   A3B2
  //   A3B3
endmodule

module SUBCIRC_DataRAMController (
  input  [15:0] SHIFT,
  input  CLK,
  output [15:0] A,
  output OE
);

  wire [15:0] adder_1_out, counter_1_q, multiplexer_1_out, multiplier_1_out;

  Counter #(.max('hffff), .trigger("falling"), .width(16)) counter_1 (
    .count(1'b1), .Q(counter_1_q), .up(1'b1), .clk(CLK));  // open: load, D, carry, clr
  Multiplier #(.width(16)) multiplier_1 (.a(counter_1_q), .b(16'h2), .out(multiplier_1_out));  // open: cin, cout
  Multiplexer #(.width(16)) multiplexer_1 (
    .in0(multiplier_1_out), .in1(adder_1_out), .out(multiplexer_1_out), .sel(CLK));
  Adder #(.width(16)) adder_1 (.a(multiplier_1_out), .b(16'h1), .out(adder_1_out));  // open: cin, cout
  Adder #(.width(16)) adder_2 (.a(SHIFT), .b(multiplexer_1_out), .out(A));  // open: cin, cout

  assign OE = 1'b1;

  // Notes on the sheet:
  //   Credits for doing with 1 counter goes to Ali
endmodule

module MatrixAdder (
  input  [63:0] B0,
  input  [63:0] B1,
  input  [63:0] B2,
  input  [63:0] B3,
  input  [63:0] A0,
  input  [63:0] A1,
  input  [63:0] A2,
  input  [63:0] A3,
  output [63:0] S0,
  output [63:0] S1,
  output [63:0] S2,
  output [63:0] S3
);

  Adder #(.width(64)) adder_1 (.a(B0), .b(A0), .out(S0));  // open: cin, cout
  Adder #(.width(64)) adder_2 (.a(B1), .b(A1), .out(S1));  // open: cin, cout
  Adder #(.width(64)) adder_3 (.a(B2), .b(A2), .out(S2));  // open: cin, cout
  Adder #(.width(64)) adder_4 (.a(B3), .b(A3), .out(S3));  // open: cin, cout

  // Notes on the sheet:
  //   Acts as a addition Node
endmodule

module Assembly (
);

  wire ACCUMULATOR_CLEAR, CLOCK_GLOBAL, EN_11_12_A, EN_11_12_B, EN_13_14_A, EN_15_16_A, EN_17_18_A,
       EN_21_22_A, EN_21_22_B, EN_23_24_A, EN_25_26_A, EN_27_28_A, EN_31_32_B, EN_41_42_B, EN_51_52_B,
       EN_61_62_B, EN_71_72_B, EN_81_82_B, ENABLE_IRAM_COUNTER, OR_WE, RESET_IRAM_COUNTER, RESET_ROM_STEP;
  wire [3:0] OP_GLOBAL, subcirc_instructionsplitter_1_flag;
  wire [7:0] STEP_COUNT, subcirc_instructionsplitter_1_addressa, subcirc_instructionsplitter_1_addressb;
  wire [15:0] counter_1_q, register_1_q, register_2_q;
  wire [15:8] controlunit_1_control_a, controlunit_1_control_b;
  wire [63:0] accumulator_1_s0, accumulator_1_s1, accumulator_1_s2, accumulator_1_s3, matrixadder_1_s0,
       matrixadder_1_s1, matrixadder_1_s2, matrixadder_1_s3, matrixadder_2_s0, matrixadder_2_s1,
       matrixadder_2_s2, matrixadder_2_s3, matrixadder_3_s0, matrixadder_3_s1, matrixadder_3_s2,
       matrixadder_3_s3, matrixadder_4_s0, matrixadder_4_s1, matrixadder_4_s2, matrixadder_4_s3,
       matrixadder_5_s0, matrixadder_5_s1, matrixadder_5_s2, matrixadder_5_s3, matrixadder_6_s0,
       matrixadder_6_s1, matrixadder_6_s2, matrixadder_6_s3, matrixadder_7_s0, matrixadder_7_s1,
       matrixadder_7_s2, matrixadder_7_s3, matrixadder_8_s0, matrixadder_8_s1, matrixadder_8_s2,
       matrixadder_8_s3, matrixadder_9_s0, matrixadder_9_s1, matrixadder_9_s2, matrixadder_9_s3,
       matrixadder_10_s0, matrixadder_10_s1, matrixadder_10_s2, matrixadder_10_s3, matrixadder_11_s0,
       matrixadder_11_s1, matrixadder_11_s2, matrixadder_11_s3, matrixadder_12_s0, matrixadder_12_s1,
       matrixadder_12_s2, matrixadder_12_s3, matrixmultiplier_1_s0, matrixmultiplier_1_s1,
       matrixmultiplier_1_s2, matrixmultiplier_1_s3, matrixmultiplier_1_w0, matrixmultiplier_1_w1,
       matrixmultiplier_1_w2, matrixmultiplier_1_w3, matrixmultiplier_2_s0, matrixmultiplier_2_s1,
       matrixmultiplier_2_s2, matrixmultiplier_2_s3, matrixmultiplier_2_w0, matrixmultiplier_2_w1,
       matrixmultiplier_2_w2, matrixmultiplier_2_w3, matrixmultiplier_3_s0, matrixmultiplier_3_s1,
       matrixmultiplier_3_s2, matrixmultiplier_3_s3, matrixmultiplier_3_w0, matrixmultiplier_3_w1,
       matrixmultiplier_3_w2, matrixmultiplier_3_w3, matrixmultiplier_4_s0, matrixmultiplier_4_s1,
       matrixmultiplier_4_s2, matrixmultiplier_4_s3, matrixmultiplier_4_w0, matrixmultiplier_4_w1,
       matrixmultiplier_4_w2, matrixmultiplier_4_w3, matrixmultiplier_5_s0, matrixmultiplier_5_s1,
       matrixmultiplier_5_s2, matrixmultiplier_5_s3, matrixmultiplier_5_w0, matrixmultiplier_5_w1,
       matrixmultiplier_5_w2, matrixmultiplier_5_w3, matrixmultiplier_6_s0, matrixmultiplier_6_s1,
       matrixmultiplier_6_s2, matrixmultiplier_6_s3, matrixmultiplier_6_w0, matrixmultiplier_6_w1,
       matrixmultiplier_6_w2, matrixmultiplier_6_w3, matrixmultiplier_7_s0, matrixmultiplier_7_s1,
       matrixmultiplier_7_s2, matrixmultiplier_7_s3, matrixmultiplier_7_w0, matrixmultiplier_7_w1,
       matrixmultiplier_7_w2, matrixmultiplier_7_w3, matrixmultiplier_8_s0, matrixmultiplier_8_s1,
       matrixmultiplier_8_s2, matrixmultiplier_8_s3, matrixmultiplier_8_w0, matrixmultiplier_8_w1,
       matrixmultiplier_8_w2, matrixmultiplier_8_w3, ram_1_dout, rambankedged_1_r0, rambankedged_1_r1,
       rambankedged_2_r0, rambankedged_2_r1, registerbankedged_1_s0, registerbankedged_1_s1,
       registerbankedged_1_s2, registerbankedged_1_s3, registerbankedged_2_s0, registerbankedged_2_s1,
       registerbankedged_2_s2, registerbankedged_2_s3, registerbankedged_3_s0, registerbankedged_3_s1,
       registerbankedged_3_s2, registerbankedged_3_s3, registerbankedged_4_s0, registerbankedged_4_s1,
       registerbankedged_4_s2, registerbankedged_4_s3, registerbankedged_5_s0, registerbankedged_5_s1,
       registerbankedged_5_s2, registerbankedged_5_s3, registerbankedged_6_s0, registerbankedged_6_s1,
       registerbankedged_6_s2, registerbankedged_6_s3, registerbankedged_7_s0, registerbankedged_7_s1,
       registerbankedged_7_s2, registerbankedged_7_s3, registerbankedged_8_s0, registerbankedged_8_s1,
       registerbankedged_8_s2, registerbankedged_8_s3, registerbankedged_9_s0, registerbankedged_9_s1,
       registerbankedged_9_s2, registerbankedged_9_s3, registerbankedged_10_s0, registerbankedged_10_s1,
       registerbankedged_10_s2, registerbankedged_10_s3, registerbankedged_11_s0, registerbankedged_11_s1,
       registerbankedged_11_s2, registerbankedged_11_s3, registerbankedged_12_s0, registerbankedged_12_s1,
       registerbankedged_12_s2, registerbankedged_12_s3, registerbankedged_13_s0, registerbankedged_13_s1,
       registerbankedged_13_s2, registerbankedged_13_s3, registerbankedged_14_s0, registerbankedged_14_s1,
       registerbankedged_14_s2, registerbankedged_14_s3, registerbankedged_15_s0, registerbankedged_15_s1,
       registerbankedged_15_s2, registerbankedged_15_s3, registerbankedged_16_s0, registerbankedged_16_s1,
       registerbankedged_16_s2, registerbankedged_16_s3, rom_1_data, S0, S1, S2, S3;

  Clock clock_1 (.out(CLOCK_GLOBAL));
  Hex_Digit_Display hex_digit_display_1 ();  // open: value, dp
  Register #(.width(16)) register_1 (.Q(register_1_q), .clk(CLOCK_GLOBAL));  // open: D, en, clr
  Register #(.width(16)) register_2 (.Q(register_2_q), .clk(CLOCK_GLOBAL));  // open: D, en, clr
  // Probe on S0
  // Probe on S2
  Counter #(.max('hffff), .width(16)) counter_1 (
    .count(ENABLE_IRAM_COUNTER), .Q(counter_1_q), .up(1'b1), .clk(CLOCK_GLOBAL), .clr(RESET_IRAM_COUNTER));  // open: load, D, carry
  // Probe on {OP_GLOBAL, STEP_COUNT}
  // Probe on S1
  // Probe on S3
  // Probe on rambankedged_1_r0
  // Probe on rambankedged_2_r0
  RAMBankEdged rambankedged_1 (
    .OFFSET(register_1_q), .CLK(CLOCK_GLOBAL), .R0(rambankedged_1_r0), .R1(rambankedged_1_r1));
  RAMBankEdged rambankedged_2 (
    .OFFSET(register_2_q), .CLK(CLOCK_GLOBAL), .R0(rambankedged_2_r0), .R1(rambankedged_2_r1));
  SUBCIRC_ROMController subcirc_romcontroller_1 (
    .RESET(RESET_ROM_STEP), .CLK(CLOCK_GLOBAL), .A(STEP_COUNT));  // open: SHIFT
  RegisterBankEdged registerbankedged_1 (
    .CLK(CLOCK_GLOBAL), .EN0(EN_11_12_A), .EN1(EN_11_12_A), .EN3(EN_21_22_A), .EN2(EN_21_22_A),
    .D(rambankedged_1_r0), .S3(registerbankedged_1_s3), .S2(registerbankedged_1_s2),
    .S1(registerbankedged_1_s1), .S0(registerbankedged_1_s0));  // open: CLEAR
  RegisterBankEdged registerbankedged_2 (
    .CLK(CLOCK_GLOBAL), .EN0(EN_13_14_A), .EN1(EN_13_14_A), .EN3(EN_23_24_A), .EN2(EN_23_24_A),
    .D(rambankedged_1_r0), .S3(registerbankedged_2_s3), .S2(registerbankedged_2_s2),
    .S1(registerbankedged_2_s1), .S0(registerbankedged_2_s0));  // open: CLEAR
  RegisterBankEdged registerbankedged_3 (
    .CLK(CLOCK_GLOBAL), .EN0(EN_15_16_A), .EN1(EN_15_16_A), .EN3(EN_25_26_A), .EN2(EN_25_26_A),
    .D(rambankedged_1_r0), .S3(registerbankedged_3_s3), .S2(registerbankedged_3_s2),
    .S1(registerbankedged_3_s1), .S0(registerbankedged_3_s0));  // open: CLEAR
  RegisterBankEdged registerbankedged_4 (
    .CLK(CLOCK_GLOBAL), .EN0(EN_17_18_A), .EN1(EN_17_18_A), .EN3(EN_27_28_A), .EN2(EN_27_28_A),
    .D(rambankedged_1_r0), .S3(registerbankedged_4_s3), .S2(registerbankedged_4_s2),
    .S1(registerbankedged_4_s1), .S0(registerbankedged_4_s0));  // open: CLEAR
  RegisterBankEdged registerbankedged_5 (
    .CLK(CLOCK_GLOBAL), .EN0(EN_11_12_A), .EN1(EN_11_12_A), .EN3(EN_21_22_A), .EN2(EN_21_22_A),
    .D(rambankedged_1_r1), .S3(registerbankedged_5_s3), .S2(registerbankedged_5_s2),
    .S1(registerbankedged_5_s1), .S0(registerbankedged_5_s0));  // open: CLEAR
  RegisterBankEdged registerbankedged_6 (
    .CLK(CLOCK_GLOBAL), .EN0(EN_13_14_A), .EN1(EN_13_14_A), .EN3(EN_23_24_A), .EN2(EN_23_24_A),
    .D(rambankedged_1_r1), .S3(registerbankedged_6_s3), .S2(registerbankedged_6_s2),
    .S1(registerbankedged_6_s1), .S0(registerbankedged_6_s0));  // open: CLEAR
  RegisterBankEdged registerbankedged_7 (
    .CLK(CLOCK_GLOBAL), .EN0(EN_15_16_A), .EN1(EN_15_16_A), .EN3(EN_25_26_A), .EN2(EN_25_26_A),
    .D(rambankedged_1_r1), .S3(registerbankedged_7_s3), .S2(registerbankedged_7_s2),
    .S1(registerbankedged_7_s1), .S0(registerbankedged_7_s0));  // open: CLEAR
  RegisterBankEdged registerbankedged_8 (
    .CLK(CLOCK_GLOBAL), .EN0(EN_17_18_A), .EN1(EN_17_18_A), .EN3(EN_27_28_A), .EN2(EN_27_28_A),
    .D(rambankedged_1_r1), .S3(registerbankedged_8_s3), .S2(registerbankedged_8_s2),
    .S1(registerbankedged_8_s1), .S0(registerbankedged_8_s0));  // open: CLEAR
  // Probe on registerbankedged_1_s3
  // Probe on registerbankedged_1_s2
  // Probe on registerbankedged_1_s1
  // Probe on registerbankedged_1_s0
  RegisterBankEdged registerbankedged_9 (
    .CLK(CLOCK_GLOBAL), .EN0(EN_11_12_B), .EN1(EN_11_12_B), .EN3(EN_21_22_B), .EN2(EN_21_22_B),
    .D(rambankedged_2_r0), .S3(registerbankedged_9_s3), .S2(registerbankedged_9_s2),
    .S1(registerbankedged_9_s1), .S0(registerbankedged_9_s0));  // open: CLEAR
  RegisterBankEdged registerbankedged_10 (
    .CLK(CLOCK_GLOBAL), .EN0(EN_31_32_B), .EN1(EN_31_32_B), .EN3(EN_41_42_B), .EN2(EN_41_42_B),
    .D(rambankedged_2_r0), .S3(registerbankedged_10_s3), .S2(registerbankedged_10_s2),
    .S1(registerbankedged_10_s1), .S0(registerbankedged_10_s0));  // open: CLEAR
  RegisterBankEdged registerbankedged_11 (
    .CLK(CLOCK_GLOBAL), .EN0(EN_51_52_B), .EN1(EN_51_52_B), .EN3(EN_61_62_B), .EN2(EN_61_62_B),
    .D(rambankedged_2_r0), .S3(registerbankedged_11_s3), .S2(registerbankedged_11_s2),
    .S1(registerbankedged_11_s1), .S0(registerbankedged_11_s0));  // open: CLEAR
  RegisterBankEdged registerbankedged_12 (
    .CLK(CLOCK_GLOBAL), .EN0(EN_71_72_B), .EN1(EN_71_72_B), .EN3(EN_81_82_B), .EN2(EN_81_82_B),
    .D(rambankedged_2_r0), .S3(registerbankedged_12_s3), .S2(registerbankedged_12_s2),
    .S1(registerbankedged_12_s1), .S0(registerbankedged_12_s0));  // open: CLEAR
  RegisterBankEdged registerbankedged_13 (
    .CLK(CLOCK_GLOBAL), .EN0(EN_11_12_B), .EN1(EN_11_12_B), .EN3(EN_21_22_B), .EN2(EN_21_22_B),
    .D(rambankedged_2_r1), .S3(registerbankedged_13_s3), .S2(registerbankedged_13_s2),
    .S1(registerbankedged_13_s1), .S0(registerbankedged_13_s0));  // open: CLEAR
  RegisterBankEdged registerbankedged_14 (
    .CLK(CLOCK_GLOBAL), .EN0(EN_31_32_B), .EN1(EN_31_32_B), .EN3(EN_41_42_B), .EN2(EN_41_42_B),
    .D(rambankedged_2_r1), .S3(registerbankedged_14_s3), .S2(registerbankedged_14_s2),
    .S1(registerbankedged_14_s1), .S0(registerbankedged_14_s0));  // open: CLEAR
  RegisterBankEdged registerbankedged_15 (
    .CLK(CLOCK_GLOBAL), .EN0(EN_51_52_B), .EN1(EN_51_52_B), .EN3(EN_61_62_B), .EN2(EN_61_62_B),
    .D(rambankedged_2_r1), .S3(registerbankedged_15_s3), .S2(registerbankedged_15_s2),
    .S1(registerbankedged_15_s1), .S0(registerbankedged_15_s0));  // open: CLEAR
  RegisterBankEdged registerbankedged_16 (
    .CLEAR(CLOCK_GLOBAL), .CLK(CLOCK_GLOBAL), .EN0(EN_71_72_B), .EN1(EN_71_72_B), .EN3(EN_81_82_B),
    .EN2(EN_81_82_B), .D(rambankedged_2_r1), .S3(registerbankedged_16_s3), .S2(registerbankedged_16_s2),
    .S1(registerbankedged_16_s1), .S0(registerbankedged_16_s0));
  ROM #(.addrWidth(12), .dataWidth(64)) rom_1 (.addr({OP_GLOBAL, STEP_COUNT}), .data(rom_1_data));
  RAM #(.addrWidth(16), .dataWidth(64), .\type ("nonvolatile")) ram_1 (
    .addr(counter_1_q), .oe(1'b1), .clk(CLOCK_GLOBAL), .dout(ram_1_dout));  // open: we, din
  MatrixMultiplier matrixmultiplier_1 (
    .A3(registerbankedged_1_s3), .A2(registerbankedged_1_s2), .A1(registerbankedged_1_s1),
    .A0(registerbankedged_1_s0), .B3(registerbankedged_9_s3), .B2(registerbankedged_9_s2),
    .B1(registerbankedged_9_s1), .B0(registerbankedged_9_s0), .S0(matrixmultiplier_1_s0),
    .S1(matrixmultiplier_1_s1), .S2(matrixmultiplier_1_s2), .S3(matrixmultiplier_1_s3),
    .W0(matrixmultiplier_1_w0), .W1(matrixmultiplier_1_w1), .W2(matrixmultiplier_1_w2),
    .W3(matrixmultiplier_1_w3));  // open: GAP
  MatrixMultiplier matrixmultiplier_2 (
    .A3(registerbankedged_2_s3), .A2(registerbankedged_2_s2), .A1(registerbankedged_2_s1),
    .A0(registerbankedged_2_s0), .B3(registerbankedged_10_s3), .B2(registerbankedged_10_s2),
    .B1(registerbankedged_10_s1), .B0(registerbankedged_10_s0), .S0(matrixmultiplier_2_s0),
    .S1(matrixmultiplier_2_s1), .S2(matrixmultiplier_2_s2), .S3(matrixmultiplier_2_s3),
    .W0(matrixmultiplier_2_w0), .W1(matrixmultiplier_2_w1), .W2(matrixmultiplier_2_w2),
    .W3(matrixmultiplier_2_w3));  // open: GAP
  MatrixMultiplier matrixmultiplier_3 (
    .A3(registerbankedged_3_s3), .A2(registerbankedged_3_s2), .A1(registerbankedged_3_s1),
    .A0(registerbankedged_3_s0), .B3(registerbankedged_11_s3), .B2(registerbankedged_11_s2),
    .B1(registerbankedged_11_s1), .B0(registerbankedged_11_s0), .S0(matrixmultiplier_3_s0),
    .S1(matrixmultiplier_3_s1), .S2(matrixmultiplier_3_s2), .S3(matrixmultiplier_3_s3),
    .W0(matrixmultiplier_3_w0), .W1(matrixmultiplier_3_w1), .W2(matrixmultiplier_3_w2),
    .W3(matrixmultiplier_3_w3));  // open: GAP
  MatrixMultiplier matrixmultiplier_4 (
    .A3(registerbankedged_4_s3), .A2(registerbankedged_4_s2), .A1(registerbankedged_4_s1),
    .A0(registerbankedged_4_s0), .B3(registerbankedged_12_s3), .B2(registerbankedged_12_s2),
    .B1(registerbankedged_12_s1), .B0(registerbankedged_12_s0), .S0(matrixmultiplier_4_s0),
    .S1(matrixmultiplier_4_s1), .S2(matrixmultiplier_4_s2), .S3(matrixmultiplier_4_s3),
    .W0(matrixmultiplier_4_w0), .W1(matrixmultiplier_4_w1), .W2(matrixmultiplier_4_w2),
    .W3(matrixmultiplier_4_w3));  // open: GAP
  MatrixMultiplier matrixmultiplier_5 (
    .A3(registerbankedged_5_s3), .A2(registerbankedged_5_s2), .A1(registerbankedged_5_s1),
    .A0(registerbankedged_5_s0), .B3(registerbankedged_13_s3), .B2(registerbankedged_13_s2),
    .B1(registerbankedged_13_s1), .B0(registerbankedged_13_s0), .S0(matrixmultiplier_5_s0),
    .S1(matrixmultiplier_5_s1), .S2(matrixmultiplier_5_s2), .S3(matrixmultiplier_5_s3),
    .W0(matrixmultiplier_5_w0), .W1(matrixmultiplier_5_w1), .W2(matrixmultiplier_5_w2),
    .W3(matrixmultiplier_5_w3));  // open: GAP
  MatrixMultiplier matrixmultiplier_6 (
    .A3(registerbankedged_6_s3), .A2(registerbankedged_6_s2), .A1(registerbankedged_6_s1),
    .A0(registerbankedged_6_s0), .B3(registerbankedged_14_s3), .B2(registerbankedged_14_s2),
    .B1(registerbankedged_14_s1), .B0(registerbankedged_14_s0), .S0(matrixmultiplier_6_s0),
    .S1(matrixmultiplier_6_s1), .S2(matrixmultiplier_6_s2), .S3(matrixmultiplier_6_s3),
    .W0(matrixmultiplier_6_w0), .W1(matrixmultiplier_6_w1), .W2(matrixmultiplier_6_w2),
    .W3(matrixmultiplier_6_w3));  // open: GAP
  MatrixMultiplier matrixmultiplier_7 (
    .A3(registerbankedged_7_s3), .A2(registerbankedged_7_s2), .A1(registerbankedged_7_s1),
    .A0(registerbankedged_7_s0), .B3(registerbankedged_15_s3), .B2(registerbankedged_15_s2),
    .B1(registerbankedged_15_s1), .B0(registerbankedged_15_s0), .S0(matrixmultiplier_7_s0),
    .S1(matrixmultiplier_7_s1), .S2(matrixmultiplier_7_s2), .S3(matrixmultiplier_7_s3),
    .W0(matrixmultiplier_7_w0), .W1(matrixmultiplier_7_w1), .W2(matrixmultiplier_7_w2),
    .W3(matrixmultiplier_7_w3));  // open: GAP
  MatrixMultiplier matrixmultiplier_8 (
    .A3(registerbankedged_8_s3), .A2(registerbankedged_8_s2), .A1(registerbankedged_8_s1),
    .A0(registerbankedged_8_s0), .B3(registerbankedged_16_s3), .B2(registerbankedged_16_s2),
    .B1(registerbankedged_16_s1), .B0(registerbankedged_16_s0), .S0(matrixmultiplier_8_s0),
    .S1(matrixmultiplier_8_s1), .S2(matrixmultiplier_8_s2), .S3(matrixmultiplier_8_s3),
    .W0(matrixmultiplier_8_w0), .W1(matrixmultiplier_8_w1), .W2(matrixmultiplier_8_w2),
    .W3(matrixmultiplier_8_w3));  // open: GAP
  // Probe on rom_1_data
  Register #(.width(4)) OuterDimA ();  // open: D, en, Q, clk, clr
  MatrixAdder matrixadder_1 (
    .B0(matrixmultiplier_1_s0), .B1(matrixmultiplier_1_s1), .B2(matrixmultiplier_1_s2),
    .B3(matrixmultiplier_1_s3), .A0(matrixmultiplier_1_w0), .A1(matrixmultiplier_1_w1),
    .A2(matrixmultiplier_1_w2), .A3(matrixmultiplier_1_w3), .S0(matrixadder_1_s0), .S1(matrixadder_1_s1),
    .S2(matrixadder_1_s2), .S3(matrixadder_1_s3));
  MatrixAdder matrixadder_2 (
    .B0(matrixmultiplier_2_s0), .B1(matrixmultiplier_2_s1), .B2(matrixmultiplier_2_s2),
    .B3(matrixmultiplier_2_s3), .A0(matrixmultiplier_2_w0), .A1(matrixmultiplier_2_w1),
    .A2(matrixmultiplier_2_w2), .A3(matrixmultiplier_2_w3), .S0(matrixadder_2_s0), .S1(matrixadder_2_s1),
    .S2(matrixadder_2_s2), .S3(matrixadder_2_s3));
  MatrixAdder matrixadder_3 (
    .B0(matrixmultiplier_3_s0), .B1(matrixmultiplier_3_s1), .B2(matrixmultiplier_3_s2),
    .B3(matrixmultiplier_3_s3), .A0(matrixmultiplier_3_w0), .A1(matrixmultiplier_3_w1),
    .A2(matrixmultiplier_3_w2), .A3(matrixmultiplier_3_w3), .S0(matrixadder_3_s0), .S1(matrixadder_3_s1),
    .S2(matrixadder_3_s2), .S3(matrixadder_3_s3));
  MatrixAdder matrixadder_4 (
    .B0(matrixmultiplier_4_s0), .B1(matrixmultiplier_4_s1), .B2(matrixmultiplier_4_s2),
    .B3(matrixmultiplier_4_s3), .A0(matrixmultiplier_4_w0), .A1(matrixmultiplier_4_w1),
    .A2(matrixmultiplier_4_w2), .A3(matrixmultiplier_4_w3), .S0(matrixadder_4_s0), .S1(matrixadder_4_s1),
    .S2(matrixadder_4_s2), .S3(matrixadder_4_s3));
  MatrixAdder matrixadder_5 (
    .B0(matrixmultiplier_5_s0), .B1(matrixmultiplier_5_s1), .B2(matrixmultiplier_5_s2),
    .B3(matrixmultiplier_5_s3), .A0(matrixmultiplier_5_w0), .A1(matrixmultiplier_5_w1),
    .A2(matrixmultiplier_5_w2), .A3(matrixmultiplier_5_w3), .S0(matrixadder_5_s0), .S1(matrixadder_5_s1),
    .S2(matrixadder_5_s2), .S3(matrixadder_5_s3));
  MatrixAdder matrixadder_6 (
    .B0(matrixmultiplier_6_s0), .B1(matrixmultiplier_6_s1), .B2(matrixmultiplier_6_s2),
    .B3(matrixmultiplier_6_s3), .A0(matrixmultiplier_6_w0), .A1(matrixmultiplier_6_w1),
    .A2(matrixmultiplier_6_w2), .A3(matrixmultiplier_6_w3), .S0(matrixadder_6_s0), .S1(matrixadder_6_s1),
    .S2(matrixadder_6_s2), .S3(matrixadder_6_s3));
  MatrixAdder matrixadder_7 (
    .B0(matrixmultiplier_7_s0), .B1(matrixmultiplier_7_s1), .B2(matrixmultiplier_7_s2),
    .B3(matrixmultiplier_7_s3), .A0(matrixmultiplier_7_w0), .A1(matrixmultiplier_7_w1),
    .A2(matrixmultiplier_7_w2), .A3(matrixmultiplier_7_w3), .S0(matrixadder_7_s0), .S1(matrixadder_7_s1),
    .S2(matrixadder_7_s2), .S3(matrixadder_7_s3));
  MatrixAdder matrixadder_8 (
    .B0(matrixmultiplier_8_s0), .B1(matrixmultiplier_8_s1), .B2(matrixmultiplier_8_s2),
    .B3(matrixmultiplier_8_s3), .A0(matrixmultiplier_8_w0), .A1(matrixmultiplier_8_w1),
    .A2(matrixmultiplier_8_w2), .A3(matrixmultiplier_8_w3), .S0(matrixadder_8_s0), .S1(matrixadder_8_s1),
    .S2(matrixadder_8_s2), .S3(matrixadder_8_s3));
  Register #(.width(4)) DIM ();  // open: D, en, Q, clk, clr
  MatrixAdder matrixadder_9 (
    .B0(matrixadder_1_s0), .B1(matrixadder_1_s1), .B2(matrixadder_1_s2), .B3(matrixadder_1_s3),
    .A0(matrixadder_2_s0), .A1(matrixadder_2_s1), .A2(matrixadder_2_s2), .A3(matrixadder_2_s3),
    .S0(matrixadder_9_s0), .S1(matrixadder_9_s1), .S2(matrixadder_9_s2), .S3(matrixadder_9_s3));
  MatrixAdder matrixadder_10 (
    .B1(matrixadder_3_s1), .B2(matrixadder_3_s2), .B3(matrixadder_3_s3), .A0(matrixadder_4_s0),
    .A1(matrixadder_4_s1), .A2(matrixadder_4_s2), .A3(matrixadder_4_s3), .S0(matrixadder_10_s0),
    .S1(matrixadder_10_s1), .S2(matrixadder_10_s2), .S3(matrixadder_10_s3));  // open: B0
  MatrixAdder matrixadder_11 (
    .B0(matrixadder_5_s0), .B1(matrixadder_5_s1), .B2(matrixadder_5_s2), .B3(matrixadder_5_s3),
    .A0(matrixadder_6_s0), .A1(matrixadder_6_s1), .A2(matrixadder_6_s2), .A3(matrixadder_6_s3),
    .S0(matrixadder_11_s0), .S1(matrixadder_11_s1), .S2(matrixadder_11_s2), .S3(matrixadder_11_s3));
  MatrixAdder matrixadder_12 (
    .B0(matrixadder_7_s0), .B1(matrixadder_7_s1), .B2(matrixadder_7_s2), .B3(matrixadder_7_s3),
    .A0(matrixadder_8_s0), .A1(matrixadder_8_s1), .A2(matrixadder_8_s2), .A3(matrixadder_8_s3),
    .S0(matrixadder_12_s0), .S1(matrixadder_12_s1), .S2(matrixadder_12_s2), .S3(matrixadder_12_s3));
  // Probe on {controlunit_1_control_a, EN_27_28_A, EN_17_18_A, EN_25_26_A, EN_15_16_A, EN_23_24_A, EN_13_14_A, EN_21_22_A, EN_11_12_A}
  Register #(.width(4)) OuterDimB ();  // open: D, en, Q, clk, clr
  ControlUnit controlunit_1 (
    .ROM_INPUT(rom_1_data), .OP(OP_GLOBAL), .FLAG(subcirc_instructionsplitter_1_flag),
    .AddressA(subcirc_instructionsplitter_1_addressa), .AddressB(subcirc_instructionsplitter_1_addressb),
    .STEP_COUNT(STEP_COUNT),
    .Control_A({controlunit_1_control_a, EN_27_28_A, EN_17_18_A, EN_25_26_A, EN_15_16_A, EN_23_24_A, EN_13_14_A, EN_21_22_A, EN_11_12_A}),
    .Control_B({controlunit_1_control_b, EN_81_82_B, EN_71_72_B, EN_61_62_B, EN_51_52_B, EN_41_42_B, EN_31_32_B, EN_21_22_B, EN_11_12_B}));
  SUBCIRC_InstructionSplitter subcirc_instructionsplitter_1 (
    .I(ram_1_dout), .AddressB(subcirc_instructionsplitter_1_addressb),
    .AddressA(subcirc_instructionsplitter_1_addressa), .OP(OP_GLOBAL),
    .Flag(subcirc_instructionsplitter_1_flag));
  Accumulator accumulator_1 (
    .Clear(ACCUMULATOR_CLEAR), .Enable(1'b1), .CLK(CLOCK_GLOBAL), .A0(matrixadder_9_s0),
    .A1(matrixadder_9_s1), .A2(matrixadder_9_s2), .A3(matrixadder_9_s3), .S0(accumulator_1_s0),
    .S1(accumulator_1_s1), .S2(accumulator_1_s2), .S3(accumulator_1_s3));
  Accumulator accumulator_2 (
    .Clear(ACCUMULATOR_CLEAR), .Enable(1'b1), .CLK(CLOCK_GLOBAL), .A0(matrixadder_10_s0),
    .A1(matrixadder_10_s1), .A2(matrixadder_10_s2), .A3(matrixadder_10_s3), .S0(accumulator_1_s0),
    .S1(accumulator_1_s1), .S2(accumulator_1_s2), .S3(accumulator_1_s3));
  Accumulator accumulator_3 (
    .Clear(ACCUMULATOR_CLEAR), .Enable(1'b1), .CLK(CLOCK_GLOBAL), .A0(matrixadder_11_s0),
    .A1(matrixadder_11_s1), .A2(matrixadder_11_s2), .A3(matrixadder_11_s3), .S0(accumulator_1_s0),
    .S1(accumulator_1_s1), .S2(accumulator_1_s2), .S3(accumulator_1_s3));
  Accumulator accumulator_4 (
    .Clear(ACCUMULATOR_CLEAR), .Enable(1'b1), .CLK(CLOCK_GLOBAL), .A0(matrixadder_12_s0),
    .A1(matrixadder_12_s1), .A2(matrixadder_12_s2), .A3(matrixadder_12_s3), .S0(accumulator_1_s0),
    .S1(accumulator_1_s1), .S2(accumulator_1_s2), .S3(accumulator_1_s3));
  RAM #(.addrWidth(16), .dataWidth(64)) ram_2 (
    .we(OR_WE), .clk(CLOCK_GLOBAL), .din(accumulator_1_s0));  // open: addr, oe, dout
  RAM #(.addrWidth(16), .dataWidth(64)) ram_3 (
    .we(OR_WE), .clk(CLOCK_GLOBAL), .din(accumulator_1_s1));  // open: addr, oe, dout
  RAM #(.addrWidth(16), .dataWidth(64)) ram_4 (
    .we(OR_WE), .clk(CLOCK_GLOBAL), .din(accumulator_1_s2));  // open: addr, oe, dout
  RAM #(.addrWidth(16), .dataWidth(64)) ram_5 (
    .we(OR_WE), .clk(CLOCK_GLOBAL), .din(accumulator_1_s3));  // open: addr, oe, dout
  RAM #(.addrWidth(16), .dataWidth(64)) ram_6 (.oe(1'b1), .clk(1'b1));  // open: addr, we, din, dout

  // Notes on the sheet:
  //   Preview
  //   Clock Counter
  //   ROM Address
  //   RAM Bank A
  //   RAM Bank B
  //   Input Bus
  //   ROM Step Counter
  //   A11 A12 A21 A22
  //   A11 A12 A21 A22
  //   8 - Bit step counter (OP+STEP_COUNT = 12 Bits) (count up to 2^12 Cycles)
  //   Register Bank A
  //   Triggered 1/2 Clock Cycle
  //   |
  //   |
  //   |
  //   |
  //   |
  //   |
  //   |
  //   |
  //   |
  //   |
  //   |
  //   |
  //   |
  //   |
  //   Control Unit
  //   Register Bank B
  //   B11 B12 B21 B22
  //   OP + Step Counter = 12 Bit
  //   contents of rom_1 (hex, n*v repeats v):
  //   1 1 4 4 10 10 40 40 2 2 8 8 20 20 80 80
  //   Instruction RAM / C
  //   (i) Should not be controlled since ENABLE_IRAM_COUNTER can be set to 0 which will hold IRAM instruction
  //   Calculate 16x16 Multiplication
  //   Micro Code ROM
  //   AW+BY+CX+DZ
  //   AW+BY+CX+DZ
  //   (i) Should have 8 Terms, but since 1 Term is a 2x2 we get 8/2 Terms
  //   1x 16x2 Row and 1x 16x2 Colmun (8 2x2) => 1 2x2
  //   A11 A12 A21 A22
  //   Unified Output Bus
  //   Unified Memory
endmodule

module DEPRECATED_ControlUnit (
  input  [63:0] ROM_INPUT,
  input  [7:0] AddressA,
  input  [7:0] AddressB,
  input  [7:0] STEP_COUNT,
  input  [3:0] OP,
  input  [3:0] FLAG
);
endmodule

module SUBCIRC_InstructionSplitter (
  input  [63:0] I,
  output [7:0] AddressB,
  output [7:0] AddressA,
  output [3:0] OP,
  output [3:0] Flag
);


  assign AddressA = I[15:8];
  assign AddressB = I[7:0];
  assign Flag = I[23:20];
  assign OP = I[19:16];

  // Notes on the sheet:
  //   Testing Splitter
endmodule

module RAMBankEdged (
  input  [15:0] OFFSET,
  input  CLK,
  output [63:0] R0,
  output [63:0] R1
);

  wire subcirc_dataramcontroller_1_oe, subcirc_dataramcontroller_2_oe;
  wire [15:0] adder_1_out, adder_2_out, subcirc_dataramcontroller_1_a, subcirc_dataramcontroller_2_a;

  SUBCIRC_DataRAMController subcirc_dataramcontroller_1 (
    .SHIFT({16{1'b0}}), .CLK(CLK), .A(subcirc_dataramcontroller_1_a), .OE(subcirc_dataramcontroller_1_oe));
  SUBCIRC_DataRAMController subcirc_dataramcontroller_2 (
    .SHIFT(16'h2), .CLK(CLK), .A(subcirc_dataramcontroller_2_a), .OE(subcirc_dataramcontroller_2_oe));
  RAM #(.addrWidth(16), .asyncread("true"), .dataWidth(64), .trigger("falling"), .\type ("nonvolatile")) ram_1 (
    .addr(adder_1_out), .oe(subcirc_dataramcontroller_1_oe), .clk(CLK), .dout(R0));  // open: we, din
  Adder #(.width(16)) adder_1 (.a(OFFSET), .b(subcirc_dataramcontroller_1_a), .out(adder_1_out));  // open: cin, cout
  RAM #(.addrWidth(16), .asyncread("true"), .dataWidth(64), .trigger("falling"), .\type ("nonvolatile")) ram_2 (
    .addr(adder_2_out), .oe(subcirc_dataramcontroller_2_oe), .clk(CLK), .dout(R1));  // open: we, din
  Adder #(.width(16)) adder_2 (.a(OFFSET), .b(subcirc_dataramcontroller_2_a), .out(adder_2_out));  // open: cin, cout

  // Other names for the same wires on the sheet: CLOCK_GLOBAL = CLK
endmodule

module RegisterBankEdged (
  input  CLEAR,
  input  CLK,
  input  EN0,
  input  EN1,
  input  EN3,
  input  EN2,
  input  [63:0] D,
  output [63:0] S3,
  output [63:0] S2,
  output [63:0] S1,
  output [63:0] S0
);

  Register #(.width(64)) register_1 (.D(D), .en(EN3), .Q(S3), .clk(CLK), .clr(CLEAR));
  Register #(.trigger("falling"), .width(64)) register_2 (.D(D), .en(EN2), .Q(S2), .clk(CLK), .clr(CLEAR));
  Register #(.width(64)) register_3 (.D(D), .en(EN1), .Q(S1), .clk(CLK), .clr(CLEAR));
  Register #(.trigger("falling"), .width(64)) register_4 (.D(D), .en(EN0), .Q(S0), .clk(CLK), .clr(CLEAR));
endmodule

module DEPECRATED_MatrixMultiplier (
  input  [63:0] B0,
  input  [63:0] A0,
  input  [63:0] B1,
  input  [63:0] A1,
  input  [63:0] B2,
  input  [63:0] A2,
  input  [63:0] B3,
  input  [63:0] A3,
  output [63:0] S0,
  output [63:0] S1,
  output [63:0] S2,
  output [63:0] S3,
  output [63:0] W0,
  output [63:0] W1,
  output [63:0] W2,
  output [63:0] W3
);

  Multiplier #(.width(64)) multiplier_1 (.a(A0), .b(B0), .out(S0));  // open: cin, cout
  Multiplier #(.width(64)) multiplier_2 (.a(A0), .b(B1), .out(S1));  // open: cin, cout
  Multiplier #(.width(64)) multiplier_3 (.a(A2), .b(B0), .out(S2));  // open: cin, cout
  Multiplier #(.width(64)) multiplier_4 (.a(A2), .b(B1), .out(S3));  // open: cin, cout
  Multiplier #(.width(64)) multiplier_5 (.a(A1), .b(B2), .out(W0));  // open: cin, cout
  Multiplier #(.width(64)) multiplier_6 (.a(A1), .b(B3), .out(W1));  // open: cin, cout
  Multiplier #(.width(64)) multiplier_7 (.a(A3), .b(B2), .out(W2));  // open: cin, cout
  Multiplier #(.width(64)) multiplier_8 (.a(A3), .b(B3), .out(W3));  // open: cin, cout

  // Notes on the sheet:
  //   Acts as a Partial Multiplication Node
  //   Supports Partial Matrix Multiplication where A*B = S1, S2 where S = S1+S2
  //   A0B0
  //   A0B1
  //   A2B0
  //   A2B1
  //   A1B2
  //   A1B3
  //   A3B2
  //   A3B3
endmodule

module ControlUnit (
  input  [63:0] ROM_INPUT,
  input  [3:0] OP,
  input  [3:0] FLAG,
  input  [7:0] AddressA,
  input  [7:0] AddressB,
  input  [7:0] STEP_COUNT,
  output [15:0] Control_A,
  output [15:0] Control_B
);


  assign Control_A = ROM_INPUT[15:0];
  assign Control_B = ROM_INPUT[31:16];
endmodule

module SCRATCHPAD (
);

  wire [3:0] controlunit_1_p4, undriven;
  wire [7:0] controlunit_1_p5, controlunit_1_p6, STEP_COUNT;
  wire [15:12] controlunit_1_p2;
  wire [63:0] ram_1_dout, rom_1_data;

  ROM #(.addrWidth(16), .dataWidth(64)) rom_1 (.addr({controlunit_1_p2, undriven, STEP_COUNT}), .data(rom_1_data));
  RAM #(.dataWidth(64)) ram_1 (.dout(ram_1_dout));  // open: addr, we, oe, clk, din
  Register #(.width(4)) DIM ();  // open: D, en, Q, clk, clr
  // ControlUnit controlunit_1: pin names not known; wires that end beside it: rom_1_data, controlunit_1_p2, controlunit_1_p2, controlunit_1_p4, controlunit_1_p5, controlunit_1_p6, STEP_COUNT
  SUBCIRC_InstructionSplitter subcirc_instructionsplitter_1 (
    .I(ram_1_dout), .AddressB(controlunit_1_p6), .AddressA(controlunit_1_p5), .OP(controlunit_1_p2),
    .Flag(controlunit_1_p4));

  // Notes on the sheet:
  //   OP + DIM + Step Counter = 16 Bit
  //   Further Optimization Based on DIM
  //   Instruction RAM / C
  //   Micro Code ROM
endmodule

module SUBCIRC_ROMController (
  input  [7:0] SHIFT,
  input  RESET,
  input  CLK,
  output [7:0] A
);

  wire [7:0] adder_1_out, counter_1_q, multiplexer_1_out, multiplier_1_out;

  Counter #(.trigger("falling")) counter_1 (
    .count(1'b1), .Q(counter_1_q), .up(1'b1), .clk(CLK), .clr(RESET));  // open: load, D, carry
  Multiplier multiplier_1 (.a(counter_1_q), .b(8'h2), .out(multiplier_1_out));  // open: cin, cout
  Multiplexer #(.width(8)) multiplexer_1 (
    .in0(multiplier_1_out), .in1(adder_1_out), .out(multiplexer_1_out), .sel(CLK));
  Adder adder_1 (.a(multiplier_1_out), .b(8'h1), .out(adder_1_out));  // open: cin, cout
  Adder adder_2 (.a(SHIFT), .b(multiplexer_1_out), .out(A));  // open: cin, cout
endmodule

module DEPRECATED_Assembly (
);

  wire ACCUMULATOR_CLEAR, CLOCK_GLOBAL, EN_11_12_A, EN_11_12_B, EN_13_14_A, EN_15_16_A, EN_17_18_A,
       EN_21_22_A, EN_21_22_B, EN_23_24_A, EN_25_26_A, EN_27_28_A, EN_31_32_B, EN_41_42_B, EN_51_52_B,
       EN_61_62_B, EN_71_72_B, EN_81_82_B, ENABLE_IRAM_COUNTER, RESET_IRAM_COUNTER, RESET_ROM_STEP;
  wire [3:0] OP_GLOBAL, subcirc_instructionsplitter_1_flag;
  wire [7:0] STEP_COUNT, subcirc_instructionsplitter_1_addressa, subcirc_instructionsplitter_1_addressb;
  wire [15:0] counter_1_q, register_1_q, register_2_q;
  wire [15:8] controlunit_1_control_a, controlunit_1_control_b;
  wire [63:0] matrixadder_1_s0, matrixadder_1_s1, matrixadder_1_s2, matrixadder_1_s3, matrixadder_2_s0,
       matrixadder_2_s1, matrixadder_2_s2, matrixadder_2_s3, matrixadder_3_s0, matrixadder_3_s1,
       matrixadder_3_s2, matrixadder_3_s3, matrixadder_4_s0, matrixadder_4_s1, matrixadder_4_s2,
       matrixadder_4_s3, matrixadder_5_s0, matrixadder_5_s1, matrixadder_5_s2, matrixadder_5_s3,
       matrixadder_6_s0, matrixadder_6_s1, matrixadder_6_s2, matrixadder_6_s3, matrixadder_7_s0,
       matrixadder_7_s1, matrixadder_7_s2, matrixadder_7_s3, matrixadder_8_s0, matrixadder_8_s1,
       matrixadder_8_s2, matrixadder_8_s3, matrixadder_9_s0, matrixadder_9_s1, matrixadder_9_s2,
       matrixadder_9_s3, matrixadder_10_s0, matrixadder_10_s1, matrixadder_10_s2, matrixadder_10_s3,
       matrixadder_11_s0, matrixadder_11_s1, matrixadder_11_s2, matrixadder_11_s3, matrixadder_12_s0,
       matrixadder_12_s1, matrixadder_12_s2, matrixadder_12_s3, matrixadder_13_s0, matrixadder_13_s1,
       matrixadder_13_s2, matrixadder_13_s3, matrixadder_14_s0, matrixadder_14_s1, matrixadder_14_s2,
       matrixadder_14_s3, matrixadder_15_s0, matrixadder_15_s1, matrixadder_15_s2, matrixadder_15_s3,
       matrixmultiplier_1_s0, matrixmultiplier_1_s1, matrixmultiplier_1_s2, matrixmultiplier_1_s3,
       matrixmultiplier_1_w0, matrixmultiplier_1_w1, matrixmultiplier_1_w2, matrixmultiplier_1_w3,
       matrixmultiplier_2_s0, matrixmultiplier_2_s1, matrixmultiplier_2_s2, matrixmultiplier_2_s3,
       matrixmultiplier_2_w0, matrixmultiplier_2_w1, matrixmultiplier_2_w2, matrixmultiplier_2_w3,
       matrixmultiplier_3_s0, matrixmultiplier_3_s1, matrixmultiplier_3_s2, matrixmultiplier_3_s3,
       matrixmultiplier_3_w0, matrixmultiplier_3_w1, matrixmultiplier_3_w2, matrixmultiplier_3_w3,
       matrixmultiplier_4_s0, matrixmultiplier_4_s1, matrixmultiplier_4_s2, matrixmultiplier_4_s3,
       matrixmultiplier_4_w0, matrixmultiplier_4_w1, matrixmultiplier_4_w2, matrixmultiplier_4_w3,
       matrixmultiplier_5_s0, matrixmultiplier_5_s1, matrixmultiplier_5_s2, matrixmultiplier_5_s3,
       matrixmultiplier_5_w0, matrixmultiplier_5_w1, matrixmultiplier_5_w2, matrixmultiplier_5_w3,
       matrixmultiplier_6_s0, matrixmultiplier_6_s1, matrixmultiplier_6_s2, matrixmultiplier_6_s3,
       matrixmultiplier_6_w0, matrixmultiplier_6_w1, matrixmultiplier_6_w2, matrixmultiplier_6_w3,
       matrixmultiplier_7_s0, matrixmultiplier_7_s1, matrixmultiplier_7_s2, matrixmultiplier_7_s3,
       matrixmultiplier_7_w0, matrixmultiplier_7_w1, matrixmultiplier_7_w2, matrixmultiplier_7_w3,
       matrixmultiplier_8_s0, matrixmultiplier_8_s1, matrixmultiplier_8_s2, matrixmultiplier_8_s3,
       matrixmultiplier_8_w0, matrixmultiplier_8_w1, matrixmultiplier_8_w2, matrixmultiplier_8_w3,
       ram_1_dout, rambankedged_1_r0, rambankedged_1_r1, rambankedged_2_r0, rambankedged_2_r1,
       registerbankedged_1_s0, registerbankedged_1_s1, registerbankedged_1_s2, registerbankedged_1_s3,
       registerbankedged_2_s0, registerbankedged_2_s1, registerbankedged_2_s2, registerbankedged_2_s3,
       registerbankedged_3_s0, registerbankedged_3_s1, registerbankedged_3_s2, registerbankedged_3_s3,
       registerbankedged_4_s0, registerbankedged_4_s1, registerbankedged_4_s2, registerbankedged_4_s3,
       registerbankedged_5_s0, registerbankedged_5_s1, registerbankedged_5_s2, registerbankedged_5_s3,
       registerbankedged_6_s0, registerbankedged_6_s1, registerbankedged_6_s2, registerbankedged_6_s3,
       registerbankedged_7_s0, registerbankedged_7_s1, registerbankedged_7_s2, registerbankedged_7_s3,
       registerbankedged_8_s0, registerbankedged_8_s1, registerbankedged_8_s2, registerbankedged_8_s3,
       registerbankedged_9_s0, registerbankedged_9_s1, registerbankedged_9_s2, registerbankedged_9_s3,
       registerbankedged_10_s0, registerbankedged_10_s1, registerbankedged_10_s2, registerbankedged_10_s3,
       registerbankedged_11_s0, registerbankedged_11_s1, registerbankedged_11_s2, registerbankedged_11_s3,
       registerbankedged_12_s0, registerbankedged_12_s1, registerbankedged_12_s2, registerbankedged_12_s3,
       registerbankedged_13_s0, registerbankedged_13_s1, registerbankedged_13_s2, registerbankedged_13_s3,
       registerbankedged_14_s0, registerbankedged_14_s1, registerbankedged_14_s2, registerbankedged_14_s3,
       registerbankedged_15_s0, registerbankedged_15_s1, registerbankedged_15_s2, registerbankedged_15_s3,
       registerbankedged_16_s0, registerbankedged_16_s1, registerbankedged_16_s2, registerbankedged_16_s3,
       rom_1_data, S0, S1, S2, S3;

  Clock clock_1 (.out(CLOCK_GLOBAL));
  Register #(.width(16)) register_1 (.Q(register_1_q), .clk(CLOCK_GLOBAL));  // open: D, en, clr
  Register #(.width(16)) register_2 (.Q(register_2_q), .clk(CLOCK_GLOBAL));  // open: D, en, clr
  // Probe on S0
  // Probe on S2
  Counter #(.max('hffff), .width(16)) counter_1 (
    .count(ENABLE_IRAM_COUNTER), .Q(counter_1_q), .up(1'b1), .clk(CLOCK_GLOBAL), .clr(RESET_IRAM_COUNTER));  // open: load, D, carry
  // Probe on {OP_GLOBAL, STEP_COUNT}
  // Probe on S1
  // Probe on S3
  // Probe on rambankedged_1_r0
  // Probe on rambankedged_2_r0
  RAMBankEdged rambankedged_1 (
    .OFFSET(register_1_q), .CLK(CLOCK_GLOBAL), .R0(rambankedged_1_r0), .R1(rambankedged_1_r1));
  RAMBankEdged rambankedged_2 (
    .OFFSET(register_2_q), .CLK(CLOCK_GLOBAL), .R0(rambankedged_2_r0), .R1(rambankedged_2_r1));
  SUBCIRC_ROMController subcirc_romcontroller_1 (
    .RESET(RESET_ROM_STEP), .CLK(CLOCK_GLOBAL), .A(STEP_COUNT));  // open: SHIFT
  RegisterBankEdged registerbankedged_1 (
    .CLK(CLOCK_GLOBAL), .EN0(EN_11_12_A), .EN1(EN_11_12_A), .EN3(EN_21_22_A), .EN2(EN_21_22_A),
    .D(rambankedged_1_r0), .S3(registerbankedged_1_s3), .S2(registerbankedged_1_s2),
    .S1(registerbankedged_1_s1), .S0(registerbankedged_1_s0));  // open: CLEAR
  RegisterBankEdged registerbankedged_2 (
    .CLK(CLOCK_GLOBAL), .EN0(EN_13_14_A), .EN1(EN_13_14_A), .EN3(EN_23_24_A), .EN2(EN_23_24_A),
    .D(rambankedged_1_r0), .S3(registerbankedged_2_s3), .S2(registerbankedged_2_s2),
    .S1(registerbankedged_2_s1), .S0(registerbankedged_2_s0));  // open: CLEAR
  RegisterBankEdged registerbankedged_3 (
    .CLK(CLOCK_GLOBAL), .EN0(EN_15_16_A), .EN1(EN_15_16_A), .EN3(EN_25_26_A), .EN2(EN_25_26_A),
    .D(rambankedged_1_r0), .S3(registerbankedged_3_s3), .S2(registerbankedged_3_s2),
    .S1(registerbankedged_3_s1), .S0(registerbankedged_3_s0));  // open: CLEAR
  RegisterBankEdged registerbankedged_4 (
    .CLK(CLOCK_GLOBAL), .EN0(EN_17_18_A), .EN1(EN_17_18_A), .EN3(EN_27_28_A), .EN2(EN_27_28_A),
    .D(rambankedged_1_r0), .S3(registerbankedged_4_s3), .S2(registerbankedged_4_s2),
    .S1(registerbankedged_4_s1), .S0(registerbankedged_4_s0));  // open: CLEAR
  RegisterBankEdged registerbankedged_5 (
    .CLK(CLOCK_GLOBAL), .EN0(EN_11_12_A), .EN1(EN_11_12_A), .EN3(EN_21_22_A), .EN2(EN_21_22_A),
    .D(rambankedged_1_r1), .S3(registerbankedged_5_s3), .S2(registerbankedged_5_s2),
    .S1(registerbankedged_5_s1), .S0(registerbankedged_5_s0));  // open: CLEAR
  RegisterBankEdged registerbankedged_6 (
    .CLK(CLOCK_GLOBAL), .EN0(EN_13_14_A), .EN1(EN_13_14_A), .EN3(EN_23_24_A), .EN2(EN_23_24_A),
    .D(rambankedged_1_r1), .S3(registerbankedged_6_s3), .S2(registerbankedged_6_s2),
    .S1(registerbankedged_6_s1), .S0(registerbankedged_6_s0));  // open: CLEAR
  RegisterBankEdged registerbankedged_7 (
    .CLK(CLOCK_GLOBAL), .EN0(EN_15_16_A), .EN1(EN_15_16_A), .EN3(EN_25_26_A), .EN2(EN_25_26_A),
    .D(rambankedged_1_r1), .S3(registerbankedged_7_s3), .S2(registerbankedged_7_s2),
    .S1(registerbankedged_7_s1), .S0(registerbankedged_7_s0));  // open: CLEAR
  RegisterBankEdged registerbankedged_8 (
    .CLK(CLOCK_GLOBAL), .EN0(EN_17_18_A), .EN1(EN_17_18_A), .EN3(EN_27_28_A), .EN2(EN_27_28_A),
    .D(rambankedged_1_r1), .S3(registerbankedged_8_s3), .S2(registerbankedged_8_s2),
    .S1(registerbankedged_8_s1), .S0(registerbankedged_8_s0));  // open: CLEAR
  // Probe on registerbankedged_1_s3
  // Probe on registerbankedged_1_s2
  // Probe on registerbankedged_1_s1
  // Probe on registerbankedged_1_s0
  RegisterBankEdged registerbankedged_9 (
    .CLK(CLOCK_GLOBAL), .EN0(EN_11_12_B), .EN1(EN_11_12_B), .EN3(EN_21_22_B), .EN2(EN_21_22_B),
    .D(rambankedged_2_r0), .S3(registerbankedged_9_s3), .S2(registerbankedged_9_s2),
    .S1(registerbankedged_9_s1), .S0(registerbankedged_9_s0));  // open: CLEAR
  RegisterBankEdged registerbankedged_10 (
    .CLK(CLOCK_GLOBAL), .EN0(EN_31_32_B), .EN1(EN_31_32_B), .EN3(EN_41_42_B), .EN2(EN_41_42_B),
    .D(rambankedged_2_r0), .S3(registerbankedged_10_s3), .S2(registerbankedged_10_s2),
    .S1(registerbankedged_10_s1), .S0(registerbankedged_10_s0));  // open: CLEAR
  RegisterBankEdged registerbankedged_11 (
    .CLK(CLOCK_GLOBAL), .EN0(EN_51_52_B), .EN1(EN_51_52_B), .EN3(EN_61_62_B), .EN2(EN_61_62_B),
    .D(rambankedged_2_r0), .S3(registerbankedged_11_s3), .S2(registerbankedged_11_s2),
    .S1(registerbankedged_11_s1), .S0(registerbankedged_11_s0));  // open: CLEAR
  RegisterBankEdged registerbankedged_12 (
    .CLK(CLOCK_GLOBAL), .EN0(EN_71_72_B), .EN1(EN_71_72_B), .EN3(EN_81_82_B), .EN2(EN_81_82_B),
    .D(rambankedged_2_r0), .S3(registerbankedged_12_s3), .S2(registerbankedged_12_s2),
    .S1(registerbankedged_12_s1), .S0(registerbankedged_12_s0));  // open: CLEAR
  RegisterBankEdged registerbankedged_13 (
    .CLK(CLOCK_GLOBAL), .EN0(EN_11_12_B), .EN1(EN_11_12_B), .EN3(EN_21_22_B), .EN2(EN_21_22_B),
    .D(rambankedged_2_r1), .S3(registerbankedged_13_s3), .S2(registerbankedged_13_s2),
    .S1(registerbankedged_13_s1), .S0(registerbankedged_13_s0));  // open: CLEAR
  RegisterBankEdged registerbankedged_14 (
    .CLK(CLOCK_GLOBAL), .EN0(EN_31_32_B), .EN1(EN_31_32_B), .EN3(EN_41_42_B), .EN2(EN_41_42_B),
    .D(rambankedged_2_r1), .S3(registerbankedged_14_s3), .S2(registerbankedged_14_s2),
    .S1(registerbankedged_14_s1), .S0(registerbankedged_14_s0));  // open: CLEAR
  RegisterBankEdged registerbankedged_15 (
    .CLK(CLOCK_GLOBAL), .EN0(EN_51_52_B), .EN1(EN_51_52_B), .EN3(EN_61_62_B), .EN2(EN_61_62_B),
    .D(rambankedged_2_r1), .S3(registerbankedged_15_s3), .S2(registerbankedged_15_s2),
    .S1(registerbankedged_15_s1), .S0(registerbankedged_15_s0));  // open: CLEAR
  RegisterBankEdged registerbankedged_16 (
    .CLEAR(CLOCK_GLOBAL), .CLK(CLOCK_GLOBAL), .EN0(EN_71_72_B), .EN1(EN_71_72_B), .EN3(EN_81_82_B),
    .EN2(EN_81_82_B), .D(rambankedged_2_r1), .S3(registerbankedged_16_s3), .S2(registerbankedged_16_s2),
    .S1(registerbankedged_16_s1), .S0(registerbankedged_16_s0));
  ROM #(.addrWidth(12), .dataWidth(64)) rom_1 (.addr({OP_GLOBAL, STEP_COUNT}), .data(rom_1_data));
  RAM #(.addrWidth(16), .dataWidth(64), .\type ("nonvolatile")) ram_1 (
    .addr(counter_1_q), .oe(1'b1), .clk(CLOCK_GLOBAL), .dout(ram_1_dout));  // open: we, din
  // Probe on rom_1_data
  // Probe on {controlunit_1_control_a, EN_27_28_A, EN_17_18_A, EN_25_26_A, EN_15_16_A, EN_23_24_A, EN_13_14_A, EN_21_22_A, EN_11_12_A}
  Register #(.width(4)) DIM ();  // open: D, en, Q, clk, clr
  MatrixMultiplier matrixmultiplier_1 (
    .A3(registerbankedged_1_s3), .A2(registerbankedged_1_s2), .A1(registerbankedged_1_s1),
    .A0(registerbankedged_1_s0), .B3(registerbankedged_9_s3), .B2(registerbankedged_9_s2),
    .B1(registerbankedged_9_s1), .B0(registerbankedged_9_s0), .S0(matrixmultiplier_1_s0),
    .S1(matrixmultiplier_1_s1), .S2(matrixmultiplier_1_s2), .S3(matrixmultiplier_1_s3),
    .W0(matrixmultiplier_1_w0), .W1(matrixmultiplier_1_w1), .W2(matrixmultiplier_1_w2),
    .W3(matrixmultiplier_1_w3));  // open: GAP
  MatrixAdder matrixadder_1 (
    .B0(matrixmultiplier_1_s0), .B1(matrixmultiplier_1_s1), .B2(matrixmultiplier_1_s2),
    .B3(matrixmultiplier_1_s3), .A0(matrixmultiplier_1_w0), .A1(matrixmultiplier_1_w1),
    .A2(matrixmultiplier_1_w2), .A3(matrixmultiplier_1_w3), .S0(matrixadder_1_s0), .S1(matrixadder_1_s1),
    .S2(matrixadder_1_s2), .S3(matrixadder_1_s3));
  MatrixMultiplier matrixmultiplier_2 (
    .A3(registerbankedged_2_s3), .A2(registerbankedged_2_s2), .A1(registerbankedged_2_s1),
    .A0(registerbankedged_2_s0), .B3(registerbankedged_10_s3), .B2(registerbankedged_10_s2),
    .B1(registerbankedged_10_s1), .B0(registerbankedged_10_s0), .S0(matrixmultiplier_2_s0),
    .S1(matrixmultiplier_2_s1), .S2(matrixmultiplier_2_s2), .S3(matrixmultiplier_2_s3),
    .W0(matrixmultiplier_2_w0), .W1(matrixmultiplier_2_w1), .W2(matrixmultiplier_2_w2),
    .W3(matrixmultiplier_2_w3));  // open: GAP
  MatrixAdder matrixadder_2 (
    .B0(matrixmultiplier_2_s0), .B1(matrixmultiplier_2_s1), .B2(matrixmultiplier_2_s2),
    .B3(matrixmultiplier_2_s3), .A0(matrixmultiplier_2_w0), .A1(matrixmultiplier_2_w1),
    .A2(matrixmultiplier_2_w2), .A3(matrixmultiplier_2_w3), .S0(matrixadder_2_s0), .S1(matrixadder_2_s1),
    .S2(matrixadder_2_s2), .S3(matrixadder_2_s3));
  MatrixMultiplier matrixmultiplier_3 (
    .A3(registerbankedged_3_s3), .A2(registerbankedged_3_s2), .A1(registerbankedged_3_s1),
    .A0(registerbankedged_3_s0), .B3(registerbankedged_11_s3), .B2(registerbankedged_11_s2),
    .B1(registerbankedged_11_s1), .B0(registerbankedged_11_s0), .S0(matrixmultiplier_3_s0),
    .S1(matrixmultiplier_3_s1), .S2(matrixmultiplier_3_s2), .S3(matrixmultiplier_3_s3),
    .W0(matrixmultiplier_3_w0), .W1(matrixmultiplier_3_w1), .W2(matrixmultiplier_3_w2),
    .W3(matrixmultiplier_3_w3));  // open: GAP
  MatrixAdder matrixadder_3 (
    .B0(matrixmultiplier_3_s0), .B1(matrixmultiplier_3_s1), .B2(matrixmultiplier_3_s2),
    .B3(matrixmultiplier_3_s3), .A0(matrixmultiplier_3_w0), .A1(matrixmultiplier_3_w1),
    .A2(matrixmultiplier_3_w2), .A3(matrixmultiplier_3_w3), .S0(matrixadder_3_s0), .S1(matrixadder_3_s1),
    .S2(matrixadder_3_s2), .S3(matrixadder_3_s3));
  MatrixMultiplier matrixmultiplier_4 (
    .A3(registerbankedged_4_s3), .A2(registerbankedged_4_s2), .A1(registerbankedged_4_s1),
    .A0(registerbankedged_4_s0), .B3(registerbankedged_12_s3), .B2(registerbankedged_12_s2),
    .B1(registerbankedged_12_s1), .B0(registerbankedged_12_s0), .S0(matrixmultiplier_4_s0),
    .S1(matrixmultiplier_4_s1), .S2(matrixmultiplier_4_s2), .S3(matrixmultiplier_4_s3),
    .W0(matrixmultiplier_4_w0), .W1(matrixmultiplier_4_w1), .W2(matrixmultiplier_4_w2),
    .W3(matrixmultiplier_4_w3));  // open: GAP
  MatrixAdder matrixadder_4 (
    .B0(matrixmultiplier_4_s0), .B1(matrixmultiplier_4_s1), .B2(matrixmultiplier_4_s2),
    .B3(matrixmultiplier_4_s3), .A0(matrixmultiplier_4_w0), .A1(matrixmultiplier_4_w1),
    .A2(matrixmultiplier_4_w2), .A3(matrixmultiplier_4_w3), .S0(matrixadder_4_s0), .S1(matrixadder_4_s1),
    .S2(matrixadder_4_s2), .S3(matrixadder_4_s3));
  MatrixMultiplier matrixmultiplier_5 (
    .A3(registerbankedged_5_s3), .A2(registerbankedged_5_s2), .A1(registerbankedged_5_s1),
    .A0(registerbankedged_5_s0), .B3(registerbankedged_13_s3), .B2(registerbankedged_13_s2),
    .B1(registerbankedged_13_s1), .B0(registerbankedged_13_s0), .S0(matrixmultiplier_5_s0),
    .S1(matrixmultiplier_5_s1), .S2(matrixmultiplier_5_s2), .S3(matrixmultiplier_5_s3),
    .W0(matrixmultiplier_5_w0), .W1(matrixmultiplier_5_w1), .W2(matrixmultiplier_5_w2),
    .W3(matrixmultiplier_5_w3));  // open: GAP
  MatrixAdder matrixadder_5 (
    .B0(matrixmultiplier_5_s0), .B1(matrixmultiplier_5_s1), .B2(matrixmultiplier_5_s2),
    .B3(matrixmultiplier_5_s3), .A0(matrixmultiplier_5_w0), .A1(matrixmultiplier_5_w1),
    .A2(matrixmultiplier_5_w2), .A3(matrixmultiplier_5_w3), .S0(matrixadder_5_s0), .S1(matrixadder_5_s1),
    .S2(matrixadder_5_s2), .S3(matrixadder_5_s3));
  MatrixMultiplier matrixmultiplier_6 (
    .A3(registerbankedged_6_s3), .A2(registerbankedged_6_s2), .A1(registerbankedged_6_s1),
    .A0(registerbankedged_6_s0), .B3(registerbankedged_14_s3), .B2(registerbankedged_14_s2),
    .B1(registerbankedged_14_s1), .B0(registerbankedged_14_s0), .S0(matrixmultiplier_6_s0),
    .S1(matrixmultiplier_6_s1), .S2(matrixmultiplier_6_s2), .S3(matrixmultiplier_6_s3),
    .W0(matrixmultiplier_6_w0), .W1(matrixmultiplier_6_w1), .W2(matrixmultiplier_6_w2),
    .W3(matrixmultiplier_6_w3));  // open: GAP
  MatrixAdder matrixadder_6 (
    .B0(matrixmultiplier_6_s0), .B1(matrixmultiplier_6_s1), .B2(matrixmultiplier_6_s2),
    .B3(matrixmultiplier_6_s3), .A0(matrixmultiplier_6_w0), .A1(matrixmultiplier_6_w1),
    .A2(matrixmultiplier_6_w2), .A3(matrixmultiplier_6_w3), .S0(matrixadder_6_s0), .S1(matrixadder_6_s1),
    .S2(matrixadder_6_s2), .S3(matrixadder_6_s3));
  MatrixMultiplier matrixmultiplier_7 (
    .A3(registerbankedged_7_s3), .A2(registerbankedged_7_s2), .A1(registerbankedged_7_s1),
    .A0(registerbankedged_7_s0), .B3(registerbankedged_15_s3), .B2(registerbankedged_15_s2),
    .B1(registerbankedged_15_s1), .B0(registerbankedged_15_s0), .S0(matrixmultiplier_7_s0),
    .S1(matrixmultiplier_7_s1), .S2(matrixmultiplier_7_s2), .S3(matrixmultiplier_7_s3),
    .W0(matrixmultiplier_7_w0), .W1(matrixmultiplier_7_w1), .W2(matrixmultiplier_7_w2),
    .W3(matrixmultiplier_7_w3));  // open: GAP
  MatrixAdder matrixadder_7 (
    .B0(matrixmultiplier_7_s0), .B1(matrixmultiplier_7_s1), .B2(matrixmultiplier_7_s2),
    .B3(matrixmultiplier_7_s3), .A0(matrixmultiplier_7_w0), .A1(matrixmultiplier_7_w1),
    .A2(matrixmultiplier_7_w2), .A3(matrixmultiplier_7_w3), .S0(matrixadder_7_s0), .S1(matrixadder_7_s1),
    .S2(matrixadder_7_s2), .S3(matrixadder_7_s3));
  MatrixMultiplier matrixmultiplier_8 (
    .A3(registerbankedged_8_s3), .A2(registerbankedged_8_s2), .A1(registerbankedged_8_s1),
    .A0(registerbankedged_8_s0), .B3(registerbankedged_16_s3), .B2(registerbankedged_16_s2),
    .B1(registerbankedged_16_s1), .B0(registerbankedged_16_s0), .S0(matrixmultiplier_8_s0),
    .S1(matrixmultiplier_8_s1), .S2(matrixmultiplier_8_s2), .S3(matrixmultiplier_8_s3),
    .W0(matrixmultiplier_8_w0), .W1(matrixmultiplier_8_w1), .W2(matrixmultiplier_8_w2),
    .W3(matrixmultiplier_8_w3));  // open: GAP
  MatrixAdder matrixadder_8 (
    .B0(matrixmultiplier_8_s0), .B1(matrixmultiplier_8_s1), .B2(matrixmultiplier_8_s2),
    .B3(matrixmultiplier_8_s3), .A0(matrixmultiplier_8_w0), .A1(matrixmultiplier_8_w1),
    .A2(matrixmultiplier_8_w2), .A3(matrixmultiplier_8_w3), .S0(matrixadder_8_s0), .S1(matrixadder_8_s1),
    .S2(matrixadder_8_s2), .S3(matrixadder_8_s3));
  ControlUnit controlunit_1 (
    .ROM_INPUT(rom_1_data), .OP(OP_GLOBAL), .FLAG(subcirc_instructionsplitter_1_flag),
    .AddressA(subcirc_instructionsplitter_1_addressa), .AddressB(subcirc_instructionsplitter_1_addressb),
    .STEP_COUNT(STEP_COUNT),
    .Control_A({controlunit_1_control_a, EN_27_28_A, EN_17_18_A, EN_25_26_A, EN_15_16_A, EN_23_24_A, EN_13_14_A, EN_21_22_A, EN_11_12_A}),
    .Control_B({controlunit_1_control_b, EN_81_82_B, EN_71_72_B, EN_61_62_B, EN_51_52_B, EN_41_42_B, EN_31_32_B, EN_21_22_B, EN_11_12_B}));
  SUBCIRC_InstructionSplitter subcirc_instructionsplitter_1 (
    .I(ram_1_dout), .AddressB(subcirc_instructionsplitter_1_addressb),
    .AddressA(subcirc_instructionsplitter_1_addressa), .OP(OP_GLOBAL),
    .Flag(subcirc_instructionsplitter_1_flag));
  MatrixAdder matrixadder_9 (
    .B0(matrixadder_1_s0), .B1(matrixadder_1_s1), .B2(matrixadder_1_s2), .B3(matrixadder_1_s3),
    .A0(matrixadder_2_s0), .A1(matrixadder_2_s1), .A2(matrixadder_2_s2), .A3(matrixadder_2_s3),
    .S0(matrixadder_9_s0), .S1(matrixadder_9_s1), .S2(matrixadder_9_s2), .S3(matrixadder_9_s3));
  MatrixAdder matrixadder_10 (
    .B0(matrixadder_3_s0), .B1(matrixadder_3_s1), .B2(matrixadder_3_s2), .B3(matrixadder_3_s3),
    .A0(matrixadder_4_s0), .A1(matrixadder_4_s1), .A2(matrixadder_4_s2), .A3(matrixadder_4_s3),
    .S0(matrixadder_10_s0), .S1(matrixadder_10_s1), .S2(matrixadder_10_s2), .S3(matrixadder_10_s3));
  MatrixAdder matrixadder_11 (
    .B0(matrixadder_5_s0), .B1(matrixadder_5_s1), .B2(matrixadder_5_s2), .B3(matrixadder_5_s3),
    .A0(matrixadder_6_s0), .A1(matrixadder_6_s1), .A2(matrixadder_6_s2), .A3(matrixadder_6_s3),
    .S0(matrixadder_11_s0), .S1(matrixadder_11_s1), .S2(matrixadder_11_s2), .S3(matrixadder_11_s3));
  MatrixAdder matrixadder_12 (
    .B0(matrixadder_7_s0), .B1(matrixadder_7_s1), .B2(matrixadder_7_s2), .B3(matrixadder_7_s3),
    .A0(matrixadder_8_s0), .A1(matrixadder_8_s1), .A2(matrixadder_8_s2), .A3(matrixadder_8_s3),
    .S0(matrixadder_12_s0), .S1(matrixadder_12_s1), .S2(matrixadder_12_s2), .S3(matrixadder_12_s3));
  MatrixAdder matrixadder_13 (
    .B0(matrixadder_9_s0), .B1(matrixadder_9_s1), .B2(matrixadder_9_s2), .B3(matrixadder_9_s3),
    .A0(matrixadder_10_s0), .A1(matrixadder_10_s1), .A2(matrixadder_10_s2), .A3(matrixadder_10_s3),
    .S0(matrixadder_13_s0), .S1(matrixadder_13_s1), .S2(matrixadder_13_s2), .S3(matrixadder_13_s3));
  MatrixAdder matrixadder_14 (
    .B0(matrixadder_11_s0), .B1(matrixadder_11_s1), .B2(matrixadder_11_s2), .B3(matrixadder_11_s3),
    .A0(matrixadder_12_s0), .A1(matrixadder_12_s1), .A2(matrixadder_12_s2), .A3(matrixadder_12_s3),
    .S0(matrixadder_14_s0), .S1(matrixadder_14_s1), .S2(matrixadder_14_s2), .S3(matrixadder_14_s3));
  MatrixAdder matrixadder_15 (
    .B0(matrixadder_13_s0), .B1(matrixadder_13_s1), .B2(matrixadder_13_s2), .B3(matrixadder_13_s3),
    .A0(matrixadder_14_s0), .A1(matrixadder_14_s1), .A2(matrixadder_14_s2), .A3(matrixadder_14_s3),
    .S0(matrixadder_15_s0), .S1(matrixadder_15_s1), .S2(matrixadder_15_s2), .S3(matrixadder_15_s3));
  Accumulator accumulator_1 (
    .Clear(ACCUMULATOR_CLEAR), .Enable(1'b1), .CLK(CLOCK_GLOBAL), .A0(matrixadder_15_s0),
    .A1(matrixadder_15_s1), .A2(matrixadder_15_s2), .A3(matrixadder_15_s3), .S0(S0), .S1(S1), .S2(S2), .S3(S3));
  Register #(.width(64)) register_3 (.D(S0), .en(1'b1), .clk(CLOCK_GLOBAL));  // open: Q, clr
  Register #(.width(64)) register_4 (.D(S2), .en(1'b1), .clk(CLOCK_GLOBAL));  // open: Q, clr
  Register #(.width(64)) register_5 (.D(S1), .en(1'b1), .clk(CLOCK_GLOBAL));  // open: Q, clr
  Register #(.width(64)) register_6 (.D(S3), .en(1'b1), .clk(CLOCK_GLOBAL));  // open: Q, clr

  // Notes on the sheet:
  //   Preview
  //   Clock Counter
  //   ROM Address
  //   RAM Bank A
  //   RAM Bank B
  //   ROM Step Counter
  //   A11 A12 A21 A22
  //   A11 A12 A21 A22
  //   8 - Bit step counter (OP+STEP_COUNT = 12 Bits) (count up to 2^12 Cycles)
  //   Register Bank A
  //   Triggered 1/2 Clock Cycle
  //   Register Bank B
  //   B11 B12 B21 B22
  //   OP + Step Counter = 12 Bit
  //   contents of rom_1 (hex, n*v repeats v):
  //   1 1 4 4 10 10 40 40 2 2 8 8 20 20 80 80
  //   Instruction RAM / C
  //   (i) Should not be controlled since ENABLE_IRAM_COUNTER can be set to 0 which will hold IRAM instruction
  //   Control Unit
  //   Micro Code ROM
  //   (i) Should have 8 Terms, but since 1 Term is a 2x2 we get 8/2 Terms
  //   Calculate 16x16 Multiplication
  //   1x 16x2 Row and 1x 16x2 Colmun (8 2x2) => 1 2x2
  //   AW+BY+CX+DZ
  //   AW+BY+CX+DZ
  //   ------------------------------------------------------------------------------------------------------------------------------------------------------------------------------------------------------
  //   Accumulator - Will reset after every cycle for 16x16 Multiplication
  //   A11 A12 A21 A22
endmodule
